# Fritzing sketch IOT_Project (saved by Fritzing 0.9.3b)
breadboards: 2

parts:
  U1 = ESP8266 NodeMCU LoLin module
  LED1 = LED - 5mm [color="Red (633nm)" package="5 mm [THT]"]
  AM1 = AM2302 Humidity and Temperature Sensor
  R1 = Temperature Sensor (Thermistor) [thermistor_type=NTC package=THT]
  R2 = Resistor [tolerance=±5% resistance=10 package="2010 [SMD]"]

nets:
  N1: U1.D4, AM1.DATA
  3V3: U1.3V3, AM1.VDD, R2.Pin_0
  GND: U1.GND, LED1.anode, AM1.GND, R1.pin_1
  N2: U1.D7, LED1.cathode
  N3: U1.A0, R1.pin_0, R2.Pin_1

custom parts:
  ESP8266 NodeMCU LoLin module: ESP8266 based NodeMCU
